# Fritzing sketch Base Machine Sequencer UI (saved by Fritzing 0.9.2b)
breadboards: 1

parts:
  U1 = mystery part, 16 pins [chip_label=CH12864F-SPI]
  RE1 = Rotary Encoder [package=THT]
  RE2 = Rotary Encoder [package=THT]
  RE3 = Rotary Encoder [package=THT]
  R1 = Resistor [tolerance=±5% resistance=100 package=THT]
  J1 = STM32 Nucleo boards

nets:
  N1: U1.pin3, J1.PB1
  N2: U1.pin4, J1.PB2
  N3: U1.pin5, J1.PB12
  N4: U1.pin6, R1.Pin_0
  N5: U1.pin7, RE1.EncoderPinC, RE2.EncoderPinC, RE3.EncoderPinC, J1.GND
  N6: U1.pin8, R1.Pin_1, J1.3V3
  N7: U1.pin9, J1.PB15
  N8: U1.pin10, J1.PB13
  N9: RE1.EncoderPinA, J1.PC5
  N10: RE1.EncoderPinB, J1.PC6
  N11: RE2.EncoderPinA, J1.PB5
  N12: RE2.EncoderPinB, J1.PB4
  N13: RE3.EncoderPinA, J1.PA10
  N14: RE3.EncoderPinB, J1.PB3

notes:
  BPM
  Pitch
  Step
  GND
  3.3V
  CH12864F-SPI
  7 SCK
  8 SI
  9 VDD
  10 VSS
  11 LEDA
  12 CS
  13 RS
  14 D/I
